# Fritzing sketch ejemploFritzing (saved by Fritzing 0.9.3b)
breadboards: 1

parts:
  Componente1 = Arduino Uno (Rev3) - ICSP
  S2 = Round Pushbutton
  LCD1 = LCD screen  # not connected
  R1 = Resistor [tolerance=±5% resistance=220 package="2010 [SMD]"]

nets:
  N1: Componente1.GND, S2.leg1
  N2: Componente1.D2, R1.Pin_0
  N3: S2.leg0, R1.Pin_1
